# Fritzing sketch blinker (saved by Fritzing 1.0.0rc)
breadboards: 1

parts:
  Part1 = Arduino Uno (Rev3)
  LED1 = smd LED [color="Red (633nm)" package="0805 [SMD]"]

nets:
  N1: Part1.D10_PWM/SS, LED1.anode
  N2: Part1.GND, LED1.cathode
